# Fritzing sketch one-octave (saved by Fritzing 0.9.4)

parts:
  Mod1 = Raspberry Pi Pico
  U2 = SK6812 RGBW LED Strip [part_number=0]
  U3 = SK6812 RGBW LED Strip
  U4 = SK6812 RGBW LED Strip
  U5 = SK6812 RGBW LED Strip
  U6 = SK6812 RGBW LED Strip
  U7 = SK6812 RGBW LED Strip
  U8 = SK6812 RGBW LED Strip
  U9 = SK6812 RGBW LED Strip
  U10 = SK6812 RGBW LED Strip
  U11 = SK6812 RGBW LED Strip
  U12 = SK6812 RGBW LED Strip
  U13 = SK6812 RGBW LED Strip
  Part1 = MPR121 Breakout

nets:
  N1: Mod1.pin_9, Part1.SDA
  N2: Mod1.pin_10, Part1.SCL
  N3: Mod1.pin_11, Part1.~IRQ
  N4: Mod1.pin_14, U2.Din
  N5: Mod1.pin_15, U3.Din
  N6: Mod1.pin_16, U4.Din
  N7: Mod1.pin_17, U5.Din
  N8: Mod1.pin_19, U6.Din
  N9: Mod1.pin_20, U7.Din
  N10: Mod1.pin_21, U8.Din
  N11: Mod1.pin_22, U9.Din
  N12: Mod1.pin_24, U10.Din
  N13: Mod1.pin_25, U11.Din
  N14: Mod1.pin_26, U12.Din
  N15: Mod1.pin_27, U13.Din
  N16: Mod1.pin_28, Mod1.pin_38, Part1.GND
  N17: Mod1.pin_36, Part1.3.3V

custom parts:
  Raspberry Pi Pico: Raspberry Pi Pico. Based around the RP2040 microcontroller the Pico is a low cost microcontroller device bringing Raspberry Pi quality, cost, and easy of use to the microcontroller space. Jan 2021, Split part in to two versions: tht (this one) and SMD. This one will drill holes for a .1 in header in pcb to allow plugging in the module as well as providing pads to solder the module to the top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
  SK6812 RGBW LED Strip: SK6812 RGBW Strip
